# Fritzing sketch Fritzing Sketch Source File (saved by Fritzing 0.9.3b)
breadboards: 1

parts:
  Part1 = Arduino Uno (Rev3)
  R1 = Resistor [tolerance=±5% resistance=220 package="0805 [SMD]"]
  R2 = Resistor [tolerance=±5% resistance=220 package="0805 [SMD]"]
  LED2 = LED - 3mm [color="Red (633nm)" package="3 mm [THT]"]
  LED3 = LED - 3mm [color="Red (633nm)" package="3 mm [THT]"]
  J1 = Piezo Speaker
  S1 = KY-026

nets:
  N1: Part1.A2, Part1.A5/SCL
  N2: Part1.GND, LED2.cathode, LED3.cathode, J1.pin1, S1.pin2
  N3: Part1.D2, J1.pin2
  N4: Part1.D3_PWM, R1.Pin_0
  N5: Part1.D4, R2.Pin_0
  N6: Part1.D7, S1.pin4
  N7: Part1.5V, S1.pin3
  N8: R1.Pin_1, LED3.anode
  N9: R2.Pin_1, LED2.anode

notes:
  Developed By Web Dev Fusion
  www.webdevfusion.com
  GND - Black
  5VC - Red
  GPIO - Blue

custom parts:
  KY-026: ky-026 flame sensor module
