# Fritzing sketch Fritzing Sketch Source File (saved by Fritzing 0.9.3b)
breadboards: 1

parts:
  Part1 = Arduino Uno (Rev3) - ICSP
  LED1 = smd LED [color="Red (633nm)" package="0805 [SMD]"]
  R1 = Resistor [tolerance=±5% resistance=220 package="2512 [SMD]"]
  J1 = Piezo Speaker

nets:
  N1: Part1.GND, LED1.cathode, J1.pin1
  N2: Part1.D4, R1.Pin_0
  N3: Part1.D5_PWM, J1.pin2
  N4: LED1.anode, R1.Pin_1

notes:
  Developed By Web Dev Fusion
  www.webdevfusion.com
  GND - Black
  5VC - Red
  GPIO - Blue
