# Fritzing sketch Fritzing Sketch Source File (saved by Fritzing 0.9.3b)
breadboards: 1

parts:
  Part1 = Arduino Uno (Rev3)
  Part2 = MQ-3 breakout
  R1 = Resistor [tolerance=±5% resistance=220 package="0805 [SMD]"]
  R2 = Resistor [tolerance=±5% resistance=220 package="0805 [SMD]"]
  LED2 = LED - 3mm [color="Red (633nm)" package="3 mm [THT]"]
  LED3 = LED - 3mm [color="Red (633nm)" package="3 mm [THT]"]
  J1 = Piezo Speaker

nets:
  N1: Part1.A2, Part1.A5/SCL, Part2.AO
  GND: Part1.GND, Part2.GND, LED2.cathode, LED3.cathode, J1.pin1
  N2: Part1.D2, J1.pin2
  N3: Part1.D3_PWM, R1.Pin_0
  N4: Part1.D4, R2.Pin_0
  5V: Part1.5V, Part2.VCC
  N5: R1.Pin_1, LED3.anode
  N6: R2.Pin_1, LED2.anode

notes:
  MQ-6
  Developed By Web Dev Fusion
  www.webdevfusion.com
  GND - Black
  5VC - Red
  GPIO - Blue

custom parts:
  MQ-3 breakout: Alcohol sensor is capable of detecting alcohol (ethanol) particles on itself and gives the information in digital form back to us to manipulate with it. SKU:101251 • Voltage: 5V DC • Power: max 750mW • Measurement range: 0.04-4mg/L
