# Fritzing sketch Fritzing Sketch Source File (saved by Fritzing 0.9.3b)
breadboards: 1

parts:
  Part1 = Arduino Uno (Rev3) - ICSP
  HC-SR04_Sensor_1 = HC-SR04 Ultrasonic Distance Sensor
  LED1 = smd LED [color="Red (633nm)" package="1206 [SMD]"]
  R1 = Resistor [tolerance=±5% resistance=220 package="0805 [SMD]"]
  J1 = Basic Servo
  J2 = Piezo Speaker

nets:
  N1: Part1.D8, J2.pin2
  N2: Part1.D3_PWM, HC-SR04_Sensor_1.TRIG
  N3: Part1.D4, HC-SR04_Sensor_1.ECHO
  N4: Part1.D5_PWM, J1.pulse
  N5: Part1.D7, R1.Pin_0
  VCC: HC-SR04_Sensor_1.VCC, J1.vcc
  GND: HC-SR04_Sensor_1.GND, LED1.cathode, J1.gnd, J2.pin1
  N6: LED1.anode, R1.Pin_1

notes:
  Developed By Web Dev Fusion
  www.webdevfusion.com
  GND - Black
  5VC - Red
  GPIO - Blue
