# Fritzing sketch Fritzing Sketch Source File (saved by Fritzing 0.9.3b)
breadboards: 1

parts:
  U1 = NodeMCU V3.0
  Part1 = BME280 Breakout
  LED1 = smd LED [color="Red (633nm)" package="1206 [SMD]"]
  R1 = Resistor [tolerance=±5% resistance=220 package="0402 [SMD]"]

nets:
  N1: U1.D0, R1.Pin_0
  N2: U1.D1, Part1.SCK/SCL
  N3: U1.D2, Part1.SDI/SDA
  3V3: U1.3V3, Part1.3.3V
  N4: U1.GND#6, U1.GND#13, U1.GND#16, U1.GND#33, Part1.GND
  N5: U1.GND#41, LED1.cathode
  N6: LED1.anode, R1.Pin_1

notes:
  Developed By Web Dev Fusion
  www.webdevfusion.com
  GND - Black
  5VC - Red
  GPIO - Blue

custom parts:
  NodeMCU V3.0: ESP8266 based NodeMCU
