# Fritzing sketch Untitled Sketch (saved by Fritzing 0.9.3b)
breadboards: 1

parts:
  U1 = NodeMCU V3.0
  U2 = 2-Channel 5v Relay Shield [package=relay-2ch5v10a]

nets:
  N1: U1.D1, U2.IN2
  N2: U1.D2, U2.IN1
  N3: U1.GND#6, U1.GND#13, U1.GND#16, U1.GND#33, U2.GND
  VIN: U1.Vin, U2.VCC

custom parts:
  NodeMCU V3.0: ESP8266 based NodeMCU
  2-Channel 5v Relay Shield: 2 Channel 5v Relay Shield w. 2x SPD-06VDC-SD-C
