# Fritzing sketch Fritzing Sketch Source File (saved by Fritzing 0.9.3b)
breadboards: 1

parts:
  U1 = NodeMCU V3.0
  U2 = 2-Channel 5v Relay Shield [package=relay-2ch5v10a]
  LED3 = LEDs [package=led10mm]
  Part3 = Lilypad Battery Connect

nets:
  N1: U1.D1, U2.IN2
  N2: U1.D2, U2.IN1
  N3: U1.GND#6, U1.GND#13, U1.GND#16, U1.GND#33, U2.GND
  VIN: U1.Vin, U2.VCC
  N4: U2.K1-In, LED3.A
  N5: U2.K1-On, Part3.+
  N6: LED3.C, Part3.-

notes:
  AC Power Source
  Developed By Web Dev Fusion
  www.webdevfusion.com
  GND - Black
  5VC - Red
  GPIO - Blue

custom parts:
  NodeMCU V3.0: ESP8266 based NodeMCU
  2-Channel 5v Relay Shield: 2 Channel 5v Relay Shield w. 2x SPD-06VDC-SD-C
  LEDs: LEDs Standard schematic elements and footprints for 5mm, 3mm, 1206, and 0603 sized LEDs. 5mm - Spark Fun Electronics SKU : COM-00529 (and others)
